# Fritzing sketch fritzing_breadboard (saved by Fritzing 0.9.3b)
circuit board: 6.92429cm x 4.39069cm
breadboards: 1

parts:
  Huzzah_Power_Binary_Sensor = Adafruit Feather HUZZAH ESP8266 [part_number="Adafruit #2821"]
  R1 = Resistor [tolerance=±5% resistance=10k package=THT]
  R2 = Resistor [tolerance=±5% resistance=5.1k package=THT]
  DS1 = DS18B20 1-Wire Temperature Sensor [part_number=DS18B20]
  R3 = Resistor [tolerance=±5% resistance=14.7k package=THT]

nets:
  N1: Huzzah_Power_Binary_Sensor.GPIO12/MISO, R1.Pin_1, R2.Pin_1
  N2: Huzzah_Power_Binary_Sensor.GPIO14/SCK, DS1.DQ, R3.Pin_0
  GND: Huzzah_Power_Binary_Sensor.GND, R2.Pin_0, DS1.GND
  3.3V: Huzzah_Power_Binary_Sensor.3.3V, DS1.VDD, R3.Pin_1
  N3: Huzzah_Power_Binary_Sensor.VBUS, R1.Pin_0

custom parts:
  Adafruit Feather HUZZAH ESP8266: his is the Adafruit Feather HUZZAH ESP8266 - our take on an 'all-in-one' ESP8266 WiFi development board with built in USB and battery charging. Its an ESP8266 WiFi module with all the extras you need, ready to rock! We have other boards in the Feather family, check'em out here. At the Feather HUZZAH's heart is an ESP8266 WiFi microcontroller clocked at 80 MHz and at 3.3V logic. This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

// code stored in the sketch: main.ino
void setup() {
  // do your stuff, like setup WiFi
}

void loop() {

    

}
